# Fritzing sketch fritzing (saved by Fritzing 0.9.2b)
breadboards: 1

parts:
  Bauteil1 = Arduino Mega 2560 (Rev3)
  Bauteil2 = HC-SR04 Ultrasonic Rangemeter

nets:
  5V: Bauteil1.5V, Bauteil2.VCC
  GND: Bauteil1.GND, Bauteil2.GND
  N1: Bauteil1.D6_PWM, Bauteil2.Echo
  N2: Bauteil1.D7_PWM, Bauteil2.Trig
